# Fritzing sketch LCD_wiring (saved by Fritzing 0.9.2b)
breadboards: 1

parts:
  Part1 = Photon
  U1 = LCD-16X2 [package=lcd-16x2_noholes]
  R1 = Resistor [tolerance=±5% resistance=100k package=THT]
  R2 = Resistor [tolerance=±5% resistance=220 package=THT]

nets:
  N1: Part1.A5, R1.Pin_1, R2.Pin_1
  GND: Part1.GND, U1.VSS, U1.VO, U1.R_W, U1.K, R1.Pin_0
  VIN: Part1.VIN, U1.VDD, U1.A
  N2: Part1.D0, U1.RS
  N3: Part1.D1, U1.E
  N4: Part1.D2, U1.DB4
  N5: Part1.D3, U1.DB5
  N6: Part1.D4, U1.DB6
  N7: Part1.D5, U1.DB7
  N8: Part1.3V3, R2.Pin_0
